// Logisim project Logisim.circ as structural Verilog: 1 circuit, main circuit main
module main (
  input  A,
  input  B,
  input  Cin,
  input  b_inv,
  input  [1:0] in_5,
  output Output,
  output Cout
);

  wire adder_1_out, and_1_out, or_1_out, xor_1_out;

  Adder #(.width(1)) adder_1 (.a(A), .b(xor_1_out), .out(adder_1_out), .cin(Cin), .cout(Cout));
  xor xor_1 (xor_1_out, B, b_inv);
  and and_1 (and_1_out, A, B);
  or or_1 (or_1_out, A, B);
  Multiplexer #(.select(2), .enable("false")) multiplexer_1 (
    .in0(and_1_out), .in1(or_1_out), .in2(adder_1_out), .in3(adder_1_out), .out(Output), .sel(in_5));
endmodule
