// Logisim project circuit.circ as structural Verilog: 1 circuit, main circuit main
module main (
  input  [31:0] A,
  input  [31:0] B,
  input  sub_ctrl,
  input  [3:0] alu_op,
  output [31:0] out_5,
  output zero_flag
);

  wire comparator_1_lt, comparator_2_lt;
  wire [31:0] adder_1_out, and_1_out, bit_extender_1_out, bit_extender_2_out, bit_extender_3_out, or_1_out,
       shifter_1_out, shifter_2_out, shifter_3_out, xor_1_out, xor_2_out;

  assign bit_extender_1_out = {{31{sub_ctrl}}, sub_ctrl};  // Bit_Extender bit_extender_1
  assign xor_1_out = B ^ bit_extender_1_out;  // XOR_Gate xor_1, 32 bits wide
  Adder #(.width(32)) adder_1 (.a(A), .b(xor_1_out), .out(adder_1_out));  // open: cin, cout
  assign and_1_out = A & B;  // AND_Gate and_1, 32 bits wide
  assign or_1_out = A | B;  // OR_Gate or_1, 32 bits wide
  assign xor_2_out = A ^ B;  // XOR_Gate xor_2, 32 bits wide
  Comparator #(.width(32)) comparator_1 (.a(A), .b(B), .lt(comparator_1_lt));  // open: gt, eq
  Comparator #(.width(32), .mode("unsigned")) comparator_2 (.a(A), .b(B), .lt(comparator_2_lt));  // open: gt, eq
  Shifter #(.width(32)) shifter_1 (.in(A), .\dist (B[4:0]), .out(shifter_1_out));
  Shifter #(.width(32), .shift("lr")) shifter_2 (.in(A), .\dist (B[4:0]), .out(shifter_2_out));
  Shifter #(.width(32), .shift("ar")) shifter_3 (.in(A), .\dist (B[4:0]), .out(shifter_3_out));
  assign bit_extender_2_out = {{31{comparator_1_lt}}, comparator_1_lt};  // Bit_Extender bit_extender_2
  assign bit_extender_3_out = {{31{comparator_2_lt}}, comparator_2_lt};  // Bit_Extender bit_extender_3
  Multiplexer #(.select(4), .width(32), .enable("false")) multiplexer_1 (
    .in0(adder_1_out), .in1(adder_1_out), .in2(and_1_out), .in3(or_1_out), .in4(xor_2_out),
    .in5(bit_extender_2_out), .in6(bit_extender_3_out), .in7(shifter_1_out), .in8(shifter_2_out),
    .in9(shifter_3_out), .out(out_5), .sel(alu_op));  // open: in10, in11, in12, in13, in14, in15
  Comparator #(.width(32)) comparator_3 (.a(out_5), .b({32{1'b0}}), .eq(zero_flag));  // open: gt, lt
endmodule
