// Logisim project Register32Bit.circ as structural Verilog: 1 circuit, main circuit main
module main (
  input  [31:0] in_1,
  output [31:0] out_2
);

  wire clk_out, ld_out, rst_out;

  Button ld (.out(ld_out));
  Register #(.width(32)) register_1 (.D(in_1), .en(ld_out), .Q(out_2), .clk(clk_out), .clr(rst_out));
  Clock clk (.out(clk_out));
  Button rst (.out(rst_out));
endmodule
